# Fritzing sketch Schaltplan (saved by Fritzing 0.9.9b)

parts:
  Bauteil1 = Arduino Uno (Rev3)
  J1 = female pin header, 6 pins [form="♀ (female)"]  # not connected
  J2 = female pin header, 6 pins [form="♀ (female)"]
  R1 = Resistor [tolerance=±5% power=0.25 resistance=10k package=THT]
  R2_(?) = Resistor [tolerance=±5% power=0.25 resistance=100k package=THT]

nets:
  N1: Bauteil1.A0, J2.pin5, R1.Pin_1
  N2: Bauteil1.A1, J2.pin4, R2_(?).Pin_1
  N3: Bauteil1.3V3, R2_(?).Pin_0
  N4: Bauteil1.5V, R1.Pin_0
  N5: Bauteil1.GND, J2.pin2, J2.pin3

notes:
  Regenmesser
  Anemometer + Windfahne
  Regenmesser und Anenometer müssen sich eine Spannungsquelle teilen, da nur 2x VCC verfügbar
  => Problem (?), weil die Spannungsabnahme des einen Messgeräts die Spannung am analogen Input des anderen Geräts beeinflusst => verfälscht Messung, Trigger des einen Messgeräts, obwohl das andere ausschlägt
  Was macht der Kondensator vor dem analogen Input des Regenmessers? Braucht das Anemometer ebenfalls einen Kondensator?
